# Fritzing sketch snesToGameCube (saved by Fritzing 0.9.3b)
breadboards: 1

parts:
  Part1 = Arduino Nano (Rev3.0)
  Part2 = Logic Level Converter
  R1 = Resistor [tolerance=±5% resistance=1k package=THT]
  J1 = female pin header, 2 pins [form="♀ (female)"]
  J2 = female pin header, 2 pins [form="♀ (female)"]
  J3 = female pin header, 2 pins [form="♀ (female)"]
  J4 = female pin header, 2 pins [form="♀ (female)"]
  J5 = female pin header, 2 pins [form="♀ (female)"]
  J6 = female pin header, 2 pins [form="♀ (female)"]
  J7 = female pin header, 2 pins [form="♀ (female)"]  # not connected
  J8 = female pin header, 2 pins [form="♀ (female)"]

nets:
  GND: Part1.GND, Part2.GND, J5.pin1, J5.pin2, J6.pin2, J8.pin1
  N1: Part1.D2, Part2.TX_HV
  N2: Part1.D3, J2.pin1, J3.pin2
  N3: Part1.D4, J1.pin1
  N4: Part1.D5, J2.pin2
  N5: Part1.5V, Part2.HV, J1.pin2, J6.pin1
  N6: Part2.LV, R1.Pin_0, J4.pin1
  N7: Part2.TX_LV, R1.Pin_1, J4.pin2

notes:
  Gamecube Connector
  5v
  GND
  3.3v
  SNES Connector
  Data
  Clock
  Latch
